// Logisim project final_project_logisim.circ as structural Verilog: 1 circuit, main circuit main
module main (
  input  clr,
  input  in_2,
  input  [1:0] in_3
);

  wire ADD_out, alu_8bit_unit_1_p3, AND_out, clk_out, decoder_1_out0, decoder_1_out1, decoder_2_out0,
       decoder_2_out1, decoder_2_out2, decoder_2_out3, HLT__FF_q, HLT_out, LDA_2_out, LDA_out, LDB_out;
  wire [1:0] IR__Reg_q_2, SC_q;
  wire [2:0] AR_q;
  wire [7:0] alu_8bit_unit_1_p1, alu_8bit_unit_1_p7, B__Reg_q, IR__Reg_q;
  wire [9:0] rom_1_data;

  Clock clk (.out(clk_out));
  D_Flip_Flop HLT__FF (.clk(clk_out), .D(in_2), .Q(HLT__FF_q), .preset(clr), .en(decoder_2_out3));  // open: Qn, reset
  and HLT (HLT_out, HLT__FF_q, decoder_1_out0);
  Decoder #(.select(2), .enable("false")) decoder_1 (
    .out0(decoder_1_out0), .out1(decoder_1_out1), .sel(SC_q));  // open: out2, out3
  Counter #(.width(2), .max('h3)) SC (
    .load(decoder_1_out1), .D(in_3), .count(HLT_out), .Q(SC_q), .clk(clk_out), .clr(clr));  // open: carry
  Decoder #(.select(2), .enable("false")) decoder_2 (
    .out0(decoder_2_out0), .out1(decoder_2_out1), .out2(decoder_2_out2), .out3(decoder_2_out3),
    .sel(IR__Reg_q_2));
  or LDA (LDA_out, decoder_2_out0, decoder_2_out1);
  Counter #(.width(3), .max('h7)) AR (.count(HLT_out), .Q(AR_q), .clk(clk_out), .clr(clr));  // open: load, D, carry
  and LDB (LDB_out, decoder_1_out1, decoder_2_out2);
  and AND (AND_out, decoder_1_out1, decoder_2_out0);
  and ADD (ADD_out, decoder_1_out1, decoder_2_out1);
  and LDA_2 (LDA_2_out, LDA_out, decoder_1_out1);
  Register B__Reg (.D(IR__Reg_q), .en(LDB_out), .Q(B__Reg_q), .clk(clk_out), .clr(clr));
  // ALU_8bit_unit alu_8bit_unit_1: pin names not known; wires that end beside it: alu_8bit_unit_1_p1, B__Reg_q, alu_8bit_unit_1_p3, alu_8bit_unit_1_p3, AND_out, ADD_out, alu_8bit_unit_1_p7
  ROM #(.addrWidth(3), .dataWidth(10)) rom_1 (.addr(AR_q), .data(rom_1_data), .sel(HLT_out));
  Register A__Reg (.D(alu_8bit_unit_1_p7), .en(LDA_2_out), .Q(alu_8bit_unit_1_p1), .clk(clk_out), .clr(clr));
  Register #(.width(10)) IR__Reg (.D(rom_1_data), .en(HLT_out), .Q({IR__Reg_q_2, IR__Reg_q}), .clk(clk_out), .clr(clr));

  // Notes on the sheet:
  //   T0 T1
  //   T
  //   D0....D3
  //   D
  //   HLT- LINE
  //   ROM
  //   contents of rom_1 (hex, n*v repeats v):
  //   11 21 45 266 6 78 98 45
endmodule
